# Fritzing sketch photon alarm circuit (saved by Fritzing 0.9.3b)
breadboards: 1

parts:
  led = smd LED [color="Red (633nm)" package="0603 [SMD]"]
  buzzer = Piezo Speaker
  Motion_sensor = PIR sensor
  photon = Photon

nets:
  GND: led.cathode, buzzer.pin1, Motion_sensor.GND, photon.GND
  N1: led.anode, photon.D7
  N2: buzzer.pin2, photon.D0
  VDD: Motion_sensor.VDD, photon.3V3
  N3: Motion_sensor.SIG, photon.D1
